// Logisim project comp.circ as structural Verilog: 15 circuits, main circuit fullAdder
module main (
  input  [2:0] in_1,
  input  [3:0] in_2,
  input  in_3,
  input  [3:0] in_4
);

  wire addALU, eALU, EIn, gRam, rA, rB, rC, sRam, wA, wB, wC;
  wire [2:0] selRam;
  wire [3:0] controlled_buffer_1_out, regmemrw_2_s, regmemrw_3_s;

  _7_Segment_Display u_7_segment_display_1 ();  // open: g, f, a, b, e, d, c, dp
  // BCD_to_7_Segment_decoder bcd_to_7_segment_decoder_1: pin names not known; wires that end beside it: in_2
  UC uc_1 (
    .send(in_3), .setRam(in_1), .cod(in_2), .wA(wA), .rA(rA), .wB(wB), .rB(rB), .eALU(eALU), .addALU(addALU),
    .ramSet(selRam), .EIn(EIn), .wC(wC), .rC(rC), .sRam(sRam), .gRam(gRam));
  assign controlled_buffer_1_out = EIn ? in_4 : 4'bz;  // Controlled_Buffer controlled_buffer_1
  regMemRW regmemrw_1 (.eW(wC), .eR(rC), .e(controlled_buffer_1_out), .s(controlled_buffer_1_out));
  regMemRW regmemrw_2 (.eW(wA), .eR(rA), .e(controlled_buffer_1_out), .s(regmemrw_2_s));
  ALU alu_1 (.B(regmemrw_3_s), .E(eALU), .add_sub(addALU), .A(regmemrw_2_s), .S(controlled_buffer_1_out));  // open: s4
  regMemRW regmemrw_3 (.eW(wB), .eR(rB), .e(controlled_buffer_1_out), .s(regmemrw_3_s));
  _7_Segment_Display u_7_segment_display_2 ();  // open: g, f, a, b, e, d, c, dp
  // BCD_to_7_Segment_decoder bcd_to_7_segment_decoder_2: pin names not known; wires that end beside it: controlled_buffer_1_out
  mem mem_1 (
    .e(controlled_buffer_1_out), .get(gRam), .set(sRam), .s2(selRam[2]), .s1(selRam[1]), .s0(selRam[0]),
    .s(controlled_buffer_1_out));
endmodule

module fullAdder (
  input  X,
  input  Y,
  input  Z,
  output S,
  output A
);

  wire and_1_out, and_2_out, xor_1_out;

  xor xor_1 (xor_1_out, Y, X);
  and and_1 (and_1_out, Y, X);
  xor xor_2 (S, Z, xor_1_out);
  and and_2 (and_2_out, Z, xor_1_out);
  or or_1 (A, and_2_out, and_1_out);
endmodule

module ALU (
  input  [3:0] A,
  input  add_sub,
  input  [3:0] B,
  input  E,
  output s4,
  output [3:0] S
);

  wire fulladder_1_a, fulladder_1_s, fulladder_2_a, fulladder_2_s, fulladder_3_a, fulladder_3_s,
       fulladder_4_a, fulladder_4_s, xor_1_out, xor_2_out, xor_3_out, xor_4_out;

  xor xor_1 (xor_1_out, add_sub, B[0]);
  xor xor_2 (xor_2_out, add_sub, B[1]);
  xor xor_3 (xor_3_out, add_sub, B[2]);
  xor xor_4 (xor_4_out, add_sub, B[3]);
  assign s4 = E ? fulladder_1_a : 1'bz;  // Controlled_Buffer controlled_buffer_1
  fullAdder fulladder_1 (.X(fulladder_2_a), .Y(A[3]), .Z(xor_4_out), .S(fulladder_1_s), .A(fulladder_1_a));
  fullAdder fulladder_2 (.X(fulladder_3_a), .Y(A[2]), .Z(xor_3_out), .S(fulladder_2_s), .A(fulladder_2_a));
  assign S[3] = E ? fulladder_1_s : 1'bz;  // Controlled_Buffer controlled_buffer_2
  assign S[2] = E ? fulladder_2_s : 1'bz;  // Controlled_Buffer controlled_buffer_3
  fullAdder fulladder_3 (.X(fulladder_4_a), .Y(A[1]), .Z(xor_2_out), .S(fulladder_3_s), .A(fulladder_3_a));
  assign S[1] = E ? fulladder_3_s : 1'bz;  // Controlled_Buffer controlled_buffer_4
  fullAdder fulladder_4 (.X(add_sub), .Y(A[0]), .Z(xor_1_out), .S(fulladder_4_s), .A(fulladder_4_a));
  assign S[0] = E ? fulladder_4_s : 1'bz;  // Controlled_Buffer controlled_buffer_5
endmodule

module UC (
  input  [2:0] setRam,
  input  [3:0] cod,
  input  send,
  output [2:0] ramSet,
  output EIn,
  output wC,
  output rC,
  output sRam,
  output gRam,
  output wA,
  output rA,
  output wB,
  output rB,
  output eALU,
  output addALU
);

  wire and_6_out;
  wire [3:0] regmemrw_1_s;

  regMemRW regmemrw_1 (.eW(send), .eR(1'b1), .e(cod), .s(regmemrw_1_s));
  and and_1 (EIn, regmemrw_1_s[0], regmemrw_1_s[1], regmemrw_1_s[2], ~regmemrw_1_s[3]);  // AND_Gate
  and and_2 (sRam, regmemrw_1_s[0], ~regmemrw_1_s[1], ~regmemrw_1_s[2], ~regmemrw_1_s[3]);  // AND_Gate
  and and_3 (gRam, ~regmemrw_1_s[0], regmemrw_1_s[1], ~regmemrw_1_s[2], ~regmemrw_1_s[3]);  // AND_Gate
  and and_4 (wA, regmemrw_1_s[0], regmemrw_1_s[1], ~regmemrw_1_s[2], ~regmemrw_1_s[3]);  // AND_Gate
  and and_5 (wB, ~regmemrw_1_s[0], ~regmemrw_1_s[1], regmemrw_1_s[2], ~regmemrw_1_s[3]);  // AND_Gate
  and and_6 (and_6_out, regmemrw_1_s[0], ~regmemrw_1_s[1], regmemrw_1_s[2], ~regmemrw_1_s[3]);  // AND_Gate
  and and_7 (addALU, ~regmemrw_1_s[0], regmemrw_1_s[1], regmemrw_1_s[2], ~regmemrw_1_s[3]);  // AND_Gate
  or or_1 (wC, and_6_out, EIn, gRam, addALU);
  or or_2 (rC, sRam, wA, wB);
  or or_3 (rA, and_6_out, addALU);
  or or_4 (rB, and_6_out, addALU);
  or or_5 (eALU, and_6_out, addALU);

  assign ramSet = setRam;
endmodule

module mem (
  input  [3:0] e,
  input  get,
  input  set,
  input  s2,
  input  s1,
  input  s0,
  output [3:0] s
);

  wire select3b_1_s0, select3b_1_s1, select3b_1_s2, select3b_1_s3, select3b_1_s4, select3b_1_s5,
       select3b_1_s6, select3b_1_s7;
  wire [3:0] controlled_buffer_1_out, regmem_1_s;

  select3b select3b_1 (
    .e2(s2), .e1(s1), .e0(s0), .s0(select3b_1_s0), .s1(select3b_1_s1), .s2(select3b_1_s2),
    .s3(select3b_1_s3), .s4(select3b_1_s4), .s5(select3b_1_s5), .s6(select3b_1_s6), .s7(select3b_1_s7));
  assign controlled_buffer_1_out = set ? e : 4'bz;  // Controlled_Buffer controlled_buffer_1
  regMem regmem_1 (.enable(select3b_1_s0), .set(set), .e(controlled_buffer_1_out), .s(regmem_1_s));
  regMem regmem_2 (.enable(select3b_1_s1), .set(set), .e(controlled_buffer_1_out), .s(regmem_1_s));
  regMem regmem_3 (.enable(select3b_1_s2), .set(set), .e(controlled_buffer_1_out), .s(regmem_1_s));
  regMem regmem_4 (.enable(select3b_1_s3), .set(set), .e(controlled_buffer_1_out), .s(regmem_1_s));
  regMem regmem_5 (.enable(select3b_1_s4), .set(set), .e(controlled_buffer_1_out), .s(regmem_1_s));
  regMem regmem_6 (.enable(select3b_1_s5), .set(set), .e(controlled_buffer_1_out), .s(regmem_1_s));
  regMem regmem_7 (.enable(select3b_1_s6), .set(set), .e(controlled_buffer_1_out), .s(regmem_1_s));
  regMem regmem_8 (.enable(select3b_1_s7), .set(set), .e(controlled_buffer_1_out), .s(regmem_1_s));
  assign s = get ? regmem_1_s : 4'bz;  // Controlled_Buffer controlled_buffer_2
endmodule

module regMemRW (
  input  [3:0] e,
  input  eW,
  input  eR,
  output [3:0] s
);

  wire [3:0] controlled_buffer_1_out, registro4b_1_s0;

  assign controlled_buffer_1_out = eW ? e : 4'bz;  // Controlled_Buffer controlled_buffer_1
  registro4b registro4b_1 (
    .Set(eW), .s(1'b0), .r(1'b0), .e3(controlled_buffer_1_out[3]), .e2(controlled_buffer_1_out[2]),
    .e1(controlled_buffer_1_out[1]), .e0(controlled_buffer_1_out[0]), .s3(registro4b_1_s0[3]),
    .s2(registro4b_1_s0[2]), .s1(registro4b_1_s0[1]), .s0(registro4b_1_s0[0]));
  assign s = eR ? registro4b_1_s0 : 4'bz;  // Controlled_Buffer controlled_buffer_2
endmodule

module regMem (
  input  [3:0] e,
  input  enable,
  input  set,
  output [3:0] s
);

  wire controlled_buffer_1_out;
  wire [3:0] controlled_buffer_2_out, registro4b_1_s0;

  assign controlled_buffer_1_out = enable ? set : 1'bz;  // Controlled_Buffer controlled_buffer_1
  assign controlled_buffer_2_out = enable ? e : 4'bz;  // Controlled_Buffer controlled_buffer_2
  registro4b registro4b_1 (
    .Set(controlled_buffer_1_out), .s(1'b0), .r(1'b0), .e3(controlled_buffer_2_out[3]),
    .e2(controlled_buffer_2_out[2]), .e1(controlled_buffer_2_out[1]), .e0(controlled_buffer_2_out[0]),
    .s3(registro4b_1_s0[3]), .s2(registro4b_1_s0[2]), .s1(registro4b_1_s0[1]), .s0(registro4b_1_s0[0]));
  assign s = enable ? registro4b_1_s0 : 4'bz;  // Controlled_Buffer controlled_buffer_3
endmodule

module registro4b (
  input  e3,
  input  e2,
  input  e1,
  input  e0,
  input  Set,
  input  s,
  input  r,
  output s3,
  output s2,
  output s1,
  output s0
);

  bi_D bi_d_1 (.D(e3), .CK(Set), .s1(s), .s0(r), .Q(s3));
  bi_D bi_d_2 (.D(e2), .CK(Set), .s1(s), .s0(r), .Q(s2));
  bi_D bi_d_3 (.D(e1), .CK(Set), .s1(s), .s0(r), .Q(s1));
  bi_D bi_d_4 (.D(e0), .CK(Set), .s1(s), .s0(r), .Q(s0));
endmodule

module select3b (
  input  e2,
  input  e1,
  input  e0,
  output s0,
  output s1,
  output s2,
  output s3,
  output s4,
  output s5,
  output s6,
  output s7
);

  and and_1 (s0, ~e0, ~e1, ~e2);  // AND_Gate
  and and_2 (s1, e0, ~e1, ~e2);  // AND_Gate
  and and_3 (s2, ~e0, e1, ~e2);  // AND_Gate
  and and_4 (s3, e0, e1, ~e2);  // AND_Gate
  and and_5 (s4, ~e0, ~e1, e2);  // AND_Gate
  and and_6 (s5, e0, ~e1, e2);  // AND_Gate
  and and_7 (s6, ~e0, e1, e2);  // AND_Gate
  and and_8 (s7, e0, e1, e2);
endmodule

module bi_D (
  input  s1,
  input  D,
  input  CK,
  input  s0,
  output Q
);

  wire not_1_out;

  not not_1 (not_1_out, D);
  SR_S sr_s_1 (.S(D), .R(not_1_out), .CK(CK), .s1(s1), .s0(s0), .Q(Q));
endmodule

module bi_JK (
  input  in_1,
  input  J,
  input  K,
  input  CK,
  input  in_5
);

  wire and_1_out, and_2_out, sr_ae_1_q;

  and and_1 (and_1_out, ~sr_ae_1_q, J);  // AND_Gate
  and and_2 (and_2_out, K, sr_ae_1_q);
  SR_AE sr_ae_1 (.s1(in_1), .s0(in_5), .S(and_1_out), .R(and_2_out), .CK(CK), .Q(sr_ae_1_q));
endmodule

module SR_AE (
  input  s1,
  input  S,
  input  R,
  input  CK,
  input  s0,
  output Q
);

  wire not_1_out, not_2_out, sr_s_1_q;

  SR_S sr_s_1 (.S(S), .R(R), .CK(CK), .s1(s1), .s0(s0), .Q(sr_s_1_q));
  SR_S sr_s_2 (.S(sr_s_1_q), .R(not_1_out), .CK(not_2_out), .s1(s1), .s0(s0), .Q(Q));
  not not_1 (not_1_out, sr_s_1_q);
  not not_2 (not_2_out, CK);
endmodule

module SR_S (
  input  s1,
  input  S,
  input  R,
  input  CK,
  input  s0,
  output Q
);

  wire and_1_out, and_2_out;

  and and_1 (and_1_out, S, CK);
  and and_2 (and_2_out, R, CK);
  bi_SR bi_sr_1 (.S(and_1_out), .R(and_2_out), .s1(s1), .s0(s0), .Q(Q));
endmodule

module bi_SR (
  input  s1,
  input  S,
  input  R,
  input  s0,
  output Q
);

  wire nor_1_out;

  nor nor_1 (nor_1_out, s1, S, Q);
  nor nor_2 (Q, nor_1_out, R, s0);
endmodule

module machine (
  input  [3:0] cod,
  input  in_2,
  input  [2:0] dir,
  input  [3:0] in_4
);

  wire addALU, and_6_out, eALU, EIn, gRam, rA, rB, rC, sRam, wA, wB, wC;
  wire [3:0] controlled_buffer_1_out, regmemrw_1_s, regmemrw_2_s, regmemrw_4_s;

  regMemRW regmemrw_1 (.eW(in_2), .eR(1'b1), .e(cod), .s(regmemrw_1_s));
  and and_1 (EIn, regmemrw_1_s[0], regmemrw_1_s[1], regmemrw_1_s[2], ~regmemrw_1_s[3]);  // AND_Gate
  and and_2 (sRam, regmemrw_1_s[0], ~regmemrw_1_s[1], ~regmemrw_1_s[2], ~regmemrw_1_s[3]);  // AND_Gate
  and and_3 (gRam, ~regmemrw_1_s[0], regmemrw_1_s[1], ~regmemrw_1_s[2], ~regmemrw_1_s[3]);  // AND_Gate
  and and_4 (wA, regmemrw_1_s[0], regmemrw_1_s[1], ~regmemrw_1_s[2], ~regmemrw_1_s[3]);  // AND_Gate
  and and_5 (wB, ~regmemrw_1_s[0], ~regmemrw_1_s[1], regmemrw_1_s[2], ~regmemrw_1_s[3]);  // AND_Gate
  and and_6 (and_6_out, regmemrw_1_s[0], ~regmemrw_1_s[1], regmemrw_1_s[2], ~regmemrw_1_s[3]);  // AND_Gate
  and and_7 (addALU, ~regmemrw_1_s[0], regmemrw_1_s[1], regmemrw_1_s[2], ~regmemrw_1_s[3]);  // AND_Gate
  or or_1 (wC, and_6_out, EIn, gRam, addALU);
  or or_2 (rC, sRam, wA, wB);
  or or_3 (rA, and_6_out, addALU);
  or or_4 (rB, and_6_out, addALU);
  or or_5 (eALU, and_6_out, addALU);
  assign controlled_buffer_1_out = EIn ? in_4 : 4'bz;  // Controlled_Buffer controlled_buffer_1
  regMemRW regmemrw_2 (.eW(wA), .eR(rA), .e(controlled_buffer_1_out), .s(regmemrw_2_s));
  regMemRW regmemrw_3 (.eW(wC), .eR(rC), .e(controlled_buffer_1_out), .s(controlled_buffer_1_out));
  ALU alu_1 (.B(regmemrw_4_s), .E(eALU), .add_sub(addALU), .A(regmemrw_2_s), .S(controlled_buffer_1_out));  // open: s4
  regMemRW regmemrw_4 (.eW(wB), .eR(rB), .e(controlled_buffer_1_out), .s(regmemrw_4_s));
  mem mem_1 (
    .e(controlled_buffer_1_out), .get(gRam), .set(sRam), .s2(dir[2]), .s1(dir[1]), .s0(dir[0]),
    .s(controlled_buffer_1_out));

  // Other names for the same wires on the sheet: selRam[2:0] = dir
endmodule
