// Logisim project compv2.circ as structural Verilog: 21 circuits, main circuit fullAdder
module main (
  input  [2:0] in_1,
  input  [3:0] in_2,
  input  in_3,
  input  [3:0] in_4
);

  wire addALU, eALU, EIn, gRam, rA, rB, rC, sRam, wA, wB, wC;
  wire [2:0] selRam;
  wire [3:0] controlled_buffer_1_out, regmemrw_2_s, regmemrw_3_s;

  _7_Segment_Display u_7_segment_display_1 ();  // open: g, f, a, b, e, d, c, dp
  // BCD_to_7_Segment_decoder bcd_to_7_segment_decoder_1: pin names not known; wires that end beside it: in_2
  UC uc_1 (
    .send(in_3), .setRam(in_1), .cod(in_2), .wA(wA), .rA(rA), .wB(wB), .rB(rB), .eALU(eALU), .addALU(addALU),
    .ramSet(selRam), .EIn(EIn), .wC(wC), .rC(rC), .sRam(sRam), .gRam(gRam));
  assign controlled_buffer_1_out = EIn ? in_4 : 4'bz;  // Controlled_Buffer controlled_buffer_1
  regMemRW regmemrw_1 (.eW(wC), .eR(rC), .e(controlled_buffer_1_out), .s(controlled_buffer_1_out));
  regMemRW regmemrw_2 (.eW(wA), .eR(rA), .e(controlled_buffer_1_out), .s(regmemrw_2_s));
  ALU alu_1 (.B(regmemrw_3_s), .E(eALU), .add_sub(addALU), .A(regmemrw_2_s), .S(controlled_buffer_1_out));  // open: s4
  regMemRW regmemrw_3 (.eW(wB), .eR(rB), .e(controlled_buffer_1_out), .s(regmemrw_3_s));
  _7_Segment_Display u_7_segment_display_2 ();  // open: g, f, a, b, e, d, c, dp
  // BCD_to_7_Segment_decoder bcd_to_7_segment_decoder_2: pin names not known; wires that end beside it: controlled_buffer_1_out
  mem mem_1 (
    .e(controlled_buffer_1_out), .get(gRam), .set(sRam), .s2(selRam[2]), .s1(selRam[1]), .s0(selRam[0]),
    .s(controlled_buffer_1_out));
endmodule

module fullAdder (
  input  X,
  input  Y,
  input  Z,
  output S,
  output A
);

  wire and_1_out, and_2_out, xor_1_out;

  xor xor_1 (xor_1_out, Y, X);
  and and_1 (and_1_out, Y, X);
  xor xor_2 (S, Z, xor_1_out);
  and and_2 (and_2_out, Z, xor_1_out);
  or or_1 (A, and_2_out, and_1_out);
endmodule

module ALU (
  input  [3:0] A,
  input  add_sub,
  input  [3:0] B,
  input  E,
  output s4,
  output [3:0] S
);

  wire fulladder_1_a, fulladder_1_s, fulladder_2_a, fulladder_2_s, fulladder_3_a, fulladder_3_s,
       fulladder_4_a, fulladder_4_s, xor_1_out, xor_2_out, xor_3_out, xor_4_out;

  xor xor_1 (xor_1_out, add_sub, B[0]);
  xor xor_2 (xor_2_out, add_sub, B[1]);
  xor xor_3 (xor_3_out, add_sub, B[2]);
  xor xor_4 (xor_4_out, add_sub, B[3]);
  assign s4 = E ? fulladder_1_a : 1'bz;  // Controlled_Buffer controlled_buffer_1
  fullAdder fulladder_1 (.X(fulladder_2_a), .Y(A[3]), .Z(xor_4_out), .S(fulladder_1_s), .A(fulladder_1_a));
  fullAdder fulladder_2 (.X(fulladder_3_a), .Y(A[2]), .Z(xor_3_out), .S(fulladder_2_s), .A(fulladder_2_a));
  assign S[3] = E ? fulladder_1_s : 1'bz;  // Controlled_Buffer controlled_buffer_2
  assign S[2] = E ? fulladder_2_s : 1'bz;  // Controlled_Buffer controlled_buffer_3
  fullAdder fulladder_3 (.X(fulladder_4_a), .Y(A[1]), .Z(xor_2_out), .S(fulladder_3_s), .A(fulladder_3_a));
  assign S[1] = E ? fulladder_3_s : 1'bz;  // Controlled_Buffer controlled_buffer_4
  fullAdder fulladder_4 (.X(add_sub), .Y(A[0]), .Z(xor_1_out), .S(fulladder_4_s), .A(fulladder_4_a));
  assign S[0] = E ? fulladder_4_s : 1'bz;  // Controlled_Buffer controlled_buffer_5
endmodule

module UC (
  input  [2:0] setRam,
  input  [3:0] cod,
  input  send,
  output [2:0] ramSet,
  output EIn,
  output wC,
  output rC,
  output sRam,
  output gRam,
  output wA,
  output rA,
  output wB,
  output rB,
  output eALU,
  output addALU
);

  wire and_6_out;
  wire [3:0] regmemrw_1_s;

  regMemRW regmemrw_1 (.eW(send), .eR(1'b1), .e(cod), .s(regmemrw_1_s));
  and and_1 (EIn, regmemrw_1_s[0], regmemrw_1_s[1], regmemrw_1_s[2], ~regmemrw_1_s[3]);  // AND_Gate
  and and_2 (sRam, regmemrw_1_s[0], ~regmemrw_1_s[1], ~regmemrw_1_s[2], ~regmemrw_1_s[3]);  // AND_Gate
  and and_3 (gRam, ~regmemrw_1_s[0], regmemrw_1_s[1], ~regmemrw_1_s[2], ~regmemrw_1_s[3]);  // AND_Gate
  and and_4 (wA, regmemrw_1_s[0], regmemrw_1_s[1], ~regmemrw_1_s[2], ~regmemrw_1_s[3]);  // AND_Gate
  and and_5 (wB, ~regmemrw_1_s[0], ~regmemrw_1_s[1], regmemrw_1_s[2], ~regmemrw_1_s[3]);  // AND_Gate
  and and_6 (and_6_out, regmemrw_1_s[0], ~regmemrw_1_s[1], regmemrw_1_s[2], ~regmemrw_1_s[3]);  // AND_Gate
  and and_7 (addALU, ~regmemrw_1_s[0], regmemrw_1_s[1], regmemrw_1_s[2], ~regmemrw_1_s[3]);  // AND_Gate
  or or_1 (wC, and_6_out, EIn, gRam, addALU);
  or or_2 (rC, sRam, wA, wB);
  or or_3 (rA, and_6_out, addALU);
  or or_4 (rB, and_6_out, addALU);
  or or_5 (eALU, and_6_out, addALU);

  assign ramSet = setRam;
endmodule

module mem (
  input  [3:0] e,
  input  get,
  input  set,
  input  s2,
  input  s1,
  input  s0,
  output [3:0] s
);

  wire select3b_1_s0, select3b_1_s1, select3b_1_s2, select3b_1_s3, select3b_1_s4, select3b_1_s5,
       select3b_1_s6, select3b_1_s7;
  wire [3:0] controlled_buffer_1_out, regmem_1_s;

  select3b select3b_1 (
    .e2(s2), .e1(s1), .e0(s0), .s0(select3b_1_s0), .s1(select3b_1_s1), .s2(select3b_1_s2),
    .s3(select3b_1_s3), .s4(select3b_1_s4), .s5(select3b_1_s5), .s6(select3b_1_s6), .s7(select3b_1_s7));
  assign controlled_buffer_1_out = set ? e : 4'bz;  // Controlled_Buffer controlled_buffer_1
  regMem regmem_1 (.enable(select3b_1_s0), .set(set), .e(controlled_buffer_1_out), .s(regmem_1_s));
  regMem regmem_2 (.enable(select3b_1_s1), .set(set), .e(controlled_buffer_1_out), .s(regmem_1_s));
  regMem regmem_3 (.enable(select3b_1_s2), .set(set), .e(controlled_buffer_1_out), .s(regmem_1_s));
  regMem regmem_4 (.enable(select3b_1_s3), .set(set), .e(controlled_buffer_1_out), .s(regmem_1_s));
  regMem regmem_5 (.enable(select3b_1_s4), .set(set), .e(controlled_buffer_1_out), .s(regmem_1_s));
  regMem regmem_6 (.enable(select3b_1_s5), .set(set), .e(controlled_buffer_1_out), .s(regmem_1_s));
  regMem regmem_7 (.enable(select3b_1_s6), .set(set), .e(controlled_buffer_1_out), .s(regmem_1_s));
  regMem regmem_8 (.enable(select3b_1_s7), .set(set), .e(controlled_buffer_1_out), .s(regmem_1_s));
  assign s = get ? regmem_1_s : 4'bz;  // Controlled_Buffer controlled_buffer_2
endmodule

module regMemRW (
  input  [3:0] e,
  input  eW,
  input  eR,
  output [3:0] s
);

  wire [3:0] controlled_buffer_1_out, registro4b_1_s0;

  assign controlled_buffer_1_out = eW ? e : 4'bz;  // Controlled_Buffer controlled_buffer_1
  registro4b registro4b_1 (
    .Set(eW), .s(1'b0), .r(1'b0), .e3(controlled_buffer_1_out[3]), .e2(controlled_buffer_1_out[2]),
    .e1(controlled_buffer_1_out[1]), .e0(controlled_buffer_1_out[0]), .s3(registro4b_1_s0[3]),
    .s2(registro4b_1_s0[2]), .s1(registro4b_1_s0[1]), .s0(registro4b_1_s0[0]));
  assign s = eR ? registro4b_1_s0 : 4'bz;  // Controlled_Buffer controlled_buffer_2
endmodule

module regMem (
  input  [3:0] e,
  input  enable,
  input  set,
  output [3:0] s
);

  wire controlled_buffer_1_out;
  wire [3:0] controlled_buffer_2_out, registro4b_1_s0;

  assign controlled_buffer_1_out = enable ? set : 1'bz;  // Controlled_Buffer controlled_buffer_1
  assign controlled_buffer_2_out = enable ? e : 4'bz;  // Controlled_Buffer controlled_buffer_2
  registro4b registro4b_1 (
    .Set(controlled_buffer_1_out), .s(1'b0), .r(1'b0), .e3(controlled_buffer_2_out[3]),
    .e2(controlled_buffer_2_out[2]), .e1(controlled_buffer_2_out[1]), .e0(controlled_buffer_2_out[0]),
    .s3(registro4b_1_s0[3]), .s2(registro4b_1_s0[2]), .s1(registro4b_1_s0[1]), .s0(registro4b_1_s0[0]));
  assign s = enable ? registro4b_1_s0 : 4'bz;  // Controlled_Buffer controlled_buffer_3
endmodule

module registro4b (
  input  e3,
  input  e2,
  input  e1,
  input  e0,
  input  Set,
  input  s,
  input  r,
  output s3,
  output s2,
  output s1,
  output s0
);

  bi_D bi_d_1 (.D(e3), .CK(Set), .s1(s), .s0(r), .Q(s3));
  bi_D bi_d_2 (.D(e2), .CK(Set), .s1(s), .s0(r), .Q(s2));
  bi_D bi_d_3 (.D(e1), .CK(Set), .s1(s), .s0(r), .Q(s1));
  bi_D bi_d_4 (.D(e0), .CK(Set), .s1(s), .s0(r), .Q(s0));
endmodule

module select3b (
  input  e2,
  input  e1,
  input  e0,
  output s0,
  output s1,
  output s2,
  output s3,
  output s4,
  output s5,
  output s6,
  output s7
);

  and and_1 (s0, ~e0, ~e1, ~e2);  // AND_Gate
  and and_2 (s1, e0, ~e1, ~e2);  // AND_Gate
  and and_3 (s2, ~e0, e1, ~e2);  // AND_Gate
  and and_4 (s3, e0, e1, ~e2);  // AND_Gate
  and and_5 (s4, ~e0, ~e1, e2);  // AND_Gate
  and and_6 (s5, e0, ~e1, e2);  // AND_Gate
  and and_7 (s6, ~e0, e1, e2);  // AND_Gate
  and and_8 (s7, e0, e1, e2);
endmodule

module bi_T (
  input  s1,
  input  T,
  input  CK,
  input  r1,
  output Q
);

  bi_JK bi_jk_1 (.J(T), .K(T), .CK(CK), .s1(s1), .r1(r1), .Q(Q));
endmodule

module bi_D (
  input  s1,
  input  D,
  input  CK,
  input  s0,
  output Q
);

  wire not_1_out;

  not not_1 (not_1_out, D);
  SR_S sr_s_1 (.S(D), .R(not_1_out), .CK(CK), .s1(s1), .s0(s0), .Q(Q));
endmodule

module bi_JK (
  input  s1,
  input  J,
  input  K,
  input  CK,
  input  r1,
  output Q
);

  wire and_1_out, and_2_out;

  and and_1 (and_1_out, ~Q, J);  // AND_Gate
  and and_2 (and_2_out, K, Q);
  SR_AE sr_ae_1 (.s1(s1), .s0(r1), .S(and_1_out), .R(and_2_out), .CK(CK), .Q(Q));
endmodule

module SR_AE (
  input  s1,
  input  S,
  input  R,
  input  CK,
  input  s0,
  output Q
);

  wire not_1_out, not_2_out, sr_s_1_q;

  SR_S sr_s_1 (.S(S), .R(R), .CK(CK), .s1(s1), .s0(s0), .Q(sr_s_1_q));
  SR_S sr_s_2 (.S(sr_s_1_q), .R(not_1_out), .CK(not_2_out), .s1(s1), .s0(s0), .Q(Q));
  not not_1 (not_1_out, sr_s_1_q);
  not not_2 (not_2_out, CK);
endmodule

module SR_S (
  input  s1,
  input  S,
  input  R,
  input  CK,
  input  s0,
  output Q
);

  wire and_1_out, and_2_out;

  and and_1 (and_1_out, S, CK);
  and and_2 (and_2_out, R, CK);
  bi_SR bi_sr_1 (.S(and_1_out), .R(and_2_out), .s1(s1), .s0(s0), .Q(Q));
endmodule

module bi_SR (
  input  s1,
  input  S,
  input  R,
  input  s0,
  output Q
);

  wire nor_1_out;

  nor nor_1 (nor_1_out, s1, S, Q);
  nor nor_2 (Q, nor_1_out, R, s0);
endmodule

module machine (
  input  [3:0] cod,
  input  in_2,
  input  [2:0] dir,
  input  [3:0] in_4
);

  wire addALU, and_6_out, eALU, EIn, gRam, rA, rB, rC, sRam, wA, wB, wC;
  wire [3:0] controlled_buffer_1_out, regmemrw_1_s, regmemrw_2_s, regmemrw_4_s;

  regMemRW regmemrw_1 (.eW(in_2), .eR(1'b1), .e(cod), .s(regmemrw_1_s));
  and and_1 (EIn, regmemrw_1_s[0], regmemrw_1_s[1], regmemrw_1_s[2], ~regmemrw_1_s[3]);  // AND_Gate
  and and_2 (sRam, regmemrw_1_s[0], ~regmemrw_1_s[1], ~regmemrw_1_s[2], ~regmemrw_1_s[3]);  // AND_Gate
  and and_3 (gRam, ~regmemrw_1_s[0], regmemrw_1_s[1], ~regmemrw_1_s[2], ~regmemrw_1_s[3]);  // AND_Gate
  and and_4 (wA, regmemrw_1_s[0], regmemrw_1_s[1], ~regmemrw_1_s[2], ~regmemrw_1_s[3]);  // AND_Gate
  and and_5 (wB, ~regmemrw_1_s[0], ~regmemrw_1_s[1], regmemrw_1_s[2], ~regmemrw_1_s[3]);  // AND_Gate
  and and_6 (and_6_out, regmemrw_1_s[0], ~regmemrw_1_s[1], regmemrw_1_s[2], ~regmemrw_1_s[3]);  // AND_Gate
  and and_7 (addALU, ~regmemrw_1_s[0], regmemrw_1_s[1], regmemrw_1_s[2], ~regmemrw_1_s[3]);  // AND_Gate
  or or_1 (wC, and_6_out, EIn, gRam, addALU);
  or or_2 (rC, sRam, wA, wB);
  or or_3 (rA, and_6_out, addALU);
  or or_4 (rB, and_6_out, addALU);
  or or_5 (eALU, and_6_out, addALU);
  assign controlled_buffer_1_out = EIn ? in_4 : 4'bz;  // Controlled_Buffer controlled_buffer_1
  regMemRW regmemrw_2 (.eW(wA), .eR(rA), .e(controlled_buffer_1_out), .s(regmemrw_2_s));
  regMemRW regmemrw_3 (.eW(wC), .eR(rC), .e(controlled_buffer_1_out), .s(controlled_buffer_1_out));
  ALU alu_1 (.B(regmemrw_4_s), .E(eALU), .add_sub(addALU), .A(regmemrw_2_s), .S(controlled_buffer_1_out));  // open: s4
  regMemRW regmemrw_4 (.eW(wB), .eR(rB), .e(controlled_buffer_1_out), .s(regmemrw_4_s));
  mem mem_1 (
    .e(controlled_buffer_1_out), .get(gRam), .set(sRam), .s2(dir[2]), .s1(dir[1]), .s0(dir[0]),
    .s(controlled_buffer_1_out));

  // Other names for the same wires on the sheet: selRam[2:0] = dir
endmodule

module ALU32 (
  input  and1,
  input  or1,
  input  not1,
  input  add1,
  input  sub1,
  input  [31:0] A,
  input  [31:0] B,
  output [31:0] S,
  output [31:0] s4
);

  wire adder_1_cout, controlled_buffer_3_out, or_1_out, or_2_out, or_3_out, or_4_out, or_5_out;
  wire [31:0] adder_1_out, and_1_out, bit_extender_1_out, controlled_buffer_1_out, controlled_buffer_2_out,
       controlled_buffer_5_out, controlled_buffer_6_out, controlled_buffer_8_out, controlled_buffer_10_out,
       controlled_buffer_11_out, not_1_out, or_6_out, xor_1_out;

  or or_1 (or_1_out, add1, sub1);
  or or_2 (or_2_out, add1, sub1);
  assign controlled_buffer_1_out = or_2_out ? B : 32'bz;  // Controlled_Buffer controlled_buffer_1
  assign bit_extender_1_out = {{31{or_3_out}}, or_3_out};  // Bit_Extender bit_extender_1
  or or_3 (or_3_out, ~add1, sub1);  // OR_Gate
  assign controlled_buffer_2_out = or_1_out ? A : 32'bz;  // Controlled_Buffer controlled_buffer_2
  assign xor_1_out = controlled_buffer_1_out ^ bit_extender_1_out;  // XOR_Gate xor_1, 32 bits wide
  or or_4 (or_4_out, add1, sub1);
  or or_5 (or_5_out, ~add1, sub1);  // OR_Gate
  Adder #(.width(32)) adder_1 (
    .a(controlled_buffer_2_out), .b(xor_1_out), .out(adder_1_out), .cin(or_5_out), .cout(adder_1_cout));
  assign controlled_buffer_3_out = or_4_out ? adder_1_cout : 1'bz;  // Controlled_Buffer controlled_buffer_3
  assign s4 = {{31{1'b0}}, controlled_buffer_3_out};  // Bit_Extender bit_extender_2
  assign S = or_4_out ? adder_1_out : 32'bz;  // Controlled_Buffer controlled_buffer_4
  assign controlled_buffer_5_out = and1 ? B : 32'bz;  // Controlled_Buffer controlled_buffer_5
  assign controlled_buffer_6_out = and1 ? A : 32'bz;  // Controlled_Buffer controlled_buffer_6
  assign and_1_out = controlled_buffer_6_out & controlled_buffer_5_out;  // AND_Gate and_1, 32 bits wide
  assign S = and1 ? and_1_out : 32'bz;  // Controlled_Buffer controlled_buffer_7
  assign controlled_buffer_8_out = or1 ? A : 32'bz;  // Controlled_Buffer controlled_buffer_8
  assign or_6_out = controlled_buffer_8_out | controlled_buffer_10_out;  // OR_Gate or_6, 32 bits wide
  assign S = or1 ? or_6_out : 32'bz;  // Controlled_Buffer controlled_buffer_9
  assign controlled_buffer_10_out = or1 ? B : 32'bz;  // Controlled_Buffer controlled_buffer_10
  assign controlled_buffer_11_out = not1 ? A : 32'bz;  // Controlled_Buffer controlled_buffer_11
  assign not_1_out = ~controlled_buffer_11_out;  // NOT_Gate not_1, 32 bits wide
  assign S = not1 ? not_1_out : 32'bz;  // Controlled_Buffer controlled_buffer_12
endmodule

module maq (
  input  [31:0] in_1
);

  wire button_1_out, button_2_out;
  wire [15:0] uc32_1_out_4;
  wire [31:0] controlled_buffer_2_out, mreg32_1_s, mreg32_3_s, ram_1_dout, uc32_1_obus;

  Clock clock_1 ();  // open: out
  Button button_1 (.out(button_1_out));
  Button button_2 (.out(button_2_out));
  UC32 uc32_1 (
    .iBUS(uc32_1_obus), .btnEnter(button_2_out), .start(button_1_out), .oBUS(uc32_1_obus),
    .out_4(uc32_1_out_4));
  assign uc32_1_obus = uc32_1_out_4[9] ? in_1 : 32'bz;  // Controlled_Buffer controlled_buffer_1
  mReg32 mreg32_1 (.eW(uc32_1_out_4[0]), .eR(1'b1), .e(uc32_1_obus), .s(mreg32_1_s));
  ALU32 alu32_1 (
    .or1(uc32_1_out_4[7]), .not1(uc32_1_out_4[8]), .A(mreg32_1_s), .B(mreg32_3_s), .add1(uc32_1_out_4[4]),
    .sub1(uc32_1_out_4[5]), .and1(uc32_1_out_4[6]), .S(uc32_1_obus));  // open: s4
  mReg32 mreg32_2 (.eW(uc32_1_out_4[3]), .eR(uc32_1_out_4[2]), .e(uc32_1_obus), .s(uc32_1_obus));
  mReg32 mreg32_3 (.eW(uc32_1_out_4[1]), .eR(1'b1), .e(uc32_1_obus), .s(mreg32_3_s));
  RAM #(.addrWidth(4), .dataWidth(32), .trigger("high")) ram_1 (
    .addr(uc32_1_out_4[15:12]), .we(uc32_1_out_4[10]), .oe(uc32_1_out_4[11]), .din(controlled_buffer_2_out),
    .dout(ram_1_dout));
  assign controlled_buffer_2_out = uc32_1_out_4[10] ? uc32_1_obus : 32'bz;  // Controlled_Buffer controlled_buffer_2
  assign uc32_1_obus = uc32_1_out_4[11] ? ram_1_dout : 32'bz;  // Controlled_Buffer controlled_buffer_3

  // Notes on the sheet:
  //   1 la memdir
  //   2 lb memdir
  //   3 sv memdir
  //   4 add
  //   5 sub
  //   6 and
  //   7 or
  //   8 not
  //   9 input
endmodule

module mReg32 (
  input  [31:0] e,
  input  eW,
  input  eR,
  output [31:0] s
);

  wire or_1_out;
  wire [31:0] controlled_buffer_1_out, register_1_q;

  assign controlled_buffer_1_out = eW ? e : 32'bz;  // Controlled_Buffer controlled_buffer_1
  Register #(.trigger("high"), .width(32)) register_1 (
    .D(controlled_buffer_1_out), .en(eW), .clk(or_1_out), .Q(register_1_q));  // open: clr
  or or_1 (or_1_out, eW, eR);
  assign s = eR ? register_1_q : 32'bz;  // Controlled_Buffer controlled_buffer_2
endmodule

module UC32 (
  input  [31:0] iBUS,
  input  start,
  input  btnEnter,
  output [15:0] out_4,
  output [31:0] oBUS
);

  wire and_1_out, and_3_out, and_4_out, and_14_out, and_15_out, and_16_out, bi_sr_1_q, clock_1_out,
       not_1_out, or_1_out, sr_s_1_q;
  wire [7:0] and_2_out, bit_extender_1_out, bit_extender_2_out, contador32_1_s0;
  wire [15:4] rom_1_data;
  wire [31:0] bit_extender_3_out, controlled_buffer_1_out;

  Clock clock_1 (.out(clock_1_out));
  and and_1 (and_1_out, ~btnEnter, sr_s_1_q);  // AND_Gate
  bi_SR bi_sr_1 (.S(btnEnter), .R(and_1_out), .s0(start), .Q(bi_sr_1_q));  // open: s1
  assign controlled_buffer_1_out = and_15_out ? iBUS : 32'bz;  // Controlled_Buffer controlled_buffer_1
  not not_1 (not_1_out, bi_sr_1_q);
  SR_S sr_s_1 (.S(bi_sr_1_q), .R(not_1_out), .CK(clock_1_out), .s0(start), .Q(sr_s_1_q));  // open: s1
  assign bit_extender_1_out = {{7{and_15_out}}, and_15_out};  // Bit_Extender bit_extender_1
  Bit_Extender #(.in_width(32), .out_width(8)) bit_extender_2 (.in(controlled_buffer_1_out), .out(bit_extender_2_out));
  or or_1 (or_1_out, sr_s_1_q, ~and_16_out);  // OR_Gate
  assign and_2_out = bit_extender_1_out & bit_extender_2_out;  // AND_Gate and_2, 8 bits wide
  and and_3 (and_3_out, clock_1_out, or_1_out);
  ROM #(.dataWidth(16)) rom_1 (.addr(contador32_1_s0), .data({rom_1_data, out_4[15:12]}));
  contador32 contador32_1 (
    .e5(and_2_out[5]), .e6(and_2_out[6]), .e7(and_2_out[7]), .r1(start), .set(and_15_out), .ck(and_3_out),
    .e0(and_2_out[0]), .e1(and_2_out[1]), .e2(and_2_out[2]), .e3(and_2_out[3]), .e4(and_2_out[4]),
    .s5(contador32_1_s0[5]), .s6(contador32_1_s0[6]), .s7(contador32_1_s0[7]), .s0(contador32_1_s0[0]),
    .s1(contador32_1_s0[1]), .s2(contador32_1_s0[2]), .s3(contador32_1_s0[3]), .s4(contador32_1_s0[4]));
  and and_4 (and_4_out, ~rom_1_data[15], ~rom_1_data[14], ~rom_1_data[13], ~rom_1_data[12]);  // AND_Gate
  and and_5 (out_4[0], ~rom_1_data[15], ~rom_1_data[14], ~rom_1_data[13], rom_1_data[12]);  // AND_Gate
  and and_6 (out_4[1], ~rom_1_data[15], ~rom_1_data[14], rom_1_data[13], ~rom_1_data[12]);  // AND_Gate
  and and_7 (out_4[2], ~rom_1_data[15], ~rom_1_data[14], rom_1_data[13], rom_1_data[12]);  // AND_Gate
  and and_8 (out_4[4], ~rom_1_data[15], rom_1_data[14], ~rom_1_data[13], ~rom_1_data[12]);  // AND_Gate
  and and_9 (out_4[5], ~rom_1_data[15], rom_1_data[14], ~rom_1_data[13], rom_1_data[12]);  // AND_Gate
  and and_10 (out_4[6], ~rom_1_data[15], rom_1_data[14], rom_1_data[13], ~rom_1_data[12]);  // AND_Gate
  assign bit_extender_3_out = {{20{1'b0}}, {rom_1_data[11:4], out_4[15:12]}};  // Bit_Extender bit_extender_3
  and and_11 (out_4[7], ~rom_1_data[15], rom_1_data[14], rom_1_data[13], rom_1_data[12]);  // AND_Gate
  assign oBUS = and_14_out ? bit_extender_3_out : 32'bz;  // Controlled_Buffer controlled_buffer_2
  and and_12 (out_4[8], rom_1_data[15], ~rom_1_data[14], ~rom_1_data[13], ~rom_1_data[12]);  // AND_Gate
  and and_13 (out_4[9], rom_1_data[15], ~rom_1_data[14], ~rom_1_data[13], rom_1_data[12]);  // AND_Gate
  and and_14 (and_14_out, rom_1_data[15], ~rom_1_data[14], rom_1_data[13], ~rom_1_data[12]);  // AND_Gate
  and and_15 (and_15_out, rom_1_data[15], ~rom_1_data[14], rom_1_data[13], rom_1_data[12]);  // AND_Gate
  and and_16 (and_16_out, rom_1_data[15], rom_1_data[14], ~rom_1_data[13], ~rom_1_data[12]);  // AND_Gate
  or or_2 (out_4[3], and_14_out, out_4[8], out_4[7], out_4[6], out_4[5], out_4[4]);
  or or_3 (out_4[11], out_4[1], out_4[0]);
  or or_4 (out_4[10], out_4[2], and_15_out, out_4[9]);

  // Notes on the sheet:
  //   1 la memdir
  //   2 lb memdir
  //   3 sv memdir
  //   4 add
  //   5 sub
  //   6 and
  //   7 or
  //   8 not
  //   9 input
  //   10 setC
  //   11 setCount
  //   12 wait
  //   contents of rom_1 (hex, n*v repeats v):
  //   c000 9001 c000 9002 c000 1001 c000 2002 c000 4000 3003 0 c000 a111 3004 a100 3005 aaaa 3006 cafe
  //   3007 edad 3008 0 0 0 a000 b000
endmodule

module contador32 (
  input  e0,
  input  e1,
  input  e2,
  input  e3,
  input  e4,
  input  e5,
  input  e6,
  input  e7,
  input  set,
  input  ck,
  input  r1,
  output s0,
  output s1,
  output s2,
  output s3,
  output s4,
  output s5,
  output s6,
  output s7
);

  wire and_1_out, and_2_out, and_3_out, and_4_out, and_5_out, and_6_out, and_7_out, and_8_out, and_9_out,
       and_10_out, and_11_out, and_12_out, and_13_out, and_14_out, and_15_out, and_16_out, and_17_out,
       and_18_out, and_19_out, and_20_out, and_21_out, and_22_out, and_23_out, or_1_out, or_2_out, or_3_out,
       or_4_out, or_5_out, or_6_out, or_7_out, or_8_out;

  and and_1 (and_1_out, set, e0);
  and and_2 (and_2_out, set, ~and_1_out);  // AND_Gate
  or or_1 (or_1_out, and_2_out, r1);
  and and_3 (and_3_out, set, ~and_5_out);  // AND_Gate
  and and_4 (and_4_out, 1'b1, s0);
  bi_T bi_t_1 (.T(1'b1), .CK(ck), .s1(and_1_out), .r1(or_1_out), .Q(s0));
  and and_5 (and_5_out, set, e1);
  bi_T bi_t_2 (.T(and_4_out), .CK(ck), .s1(and_5_out), .r1(or_2_out), .Q(s1));
  or or_2 (or_2_out, and_3_out, r1);
  and and_6 (and_6_out, set, e2);
  and and_7 (and_7_out, set, ~and_6_out);  // AND_Gate
  and and_8 (and_8_out, and_4_out, s1);
  or or_3 (or_3_out, and_7_out, r1);
  and and_9 (and_9_out, set, ~and_11_out);  // AND_Gate
  and and_10 (and_10_out, and_8_out, s2);
  bi_T bi_t_3 (.T(and_8_out), .CK(ck), .s1(and_6_out), .r1(or_3_out), .Q(s2));
  and and_11 (and_11_out, set, e3);
  bi_T bi_t_4 (.T(and_10_out), .CK(ck), .s1(and_11_out), .r1(or_4_out), .Q(s3));
  or or_4 (or_4_out, and_9_out, r1);
  and and_12 (and_12_out, set, e4);
  and and_13 (and_13_out, set, ~and_12_out);  // AND_Gate
  and and_14 (and_14_out, and_10_out, s3);
  or or_5 (or_5_out, and_13_out, r1);
  and and_15 (and_15_out, set, ~and_17_out);  // AND_Gate
  and and_16 (and_16_out, and_14_out, s4);
  bi_T bi_t_5 (.T(and_14_out), .CK(ck), .s1(and_12_out), .r1(or_5_out), .Q(s4));
  and and_17 (and_17_out, set, e5);
  bi_T bi_t_6 (.T(and_16_out), .CK(ck), .s1(and_17_out), .r1(or_6_out), .Q(s5));
  or or_6 (or_6_out, and_15_out, r1);
  and and_18 (and_18_out, set, e6);
  and and_19 (and_19_out, set, ~and_18_out);  // AND_Gate
  and and_20 (and_20_out, and_16_out, s5);
  or or_7 (or_7_out, and_19_out, r1);
  and and_21 (and_21_out, set, ~and_23_out);  // AND_Gate
  and and_22 (and_22_out, and_20_out, s6);
  bi_T bi_t_7 (.T(and_20_out), .CK(ck), .s1(and_18_out), .r1(or_7_out), .Q(s6));
  and and_23 (and_23_out, set, e7);
  bi_T bi_t_8 (.T(and_22_out), .CK(ck), .s1(and_23_out), .r1(or_8_out), .Q(s7));
  or or_8 (or_8_out, and_21_out, r1);
endmodule
